# Fritzing sketch mega_HC-SR04 (saved by Fritzing 0.9.3b)

parts:
  부품1 = Arduino Mega 2560 (Rev3)
  hc-sr1 = hc-sr04

nets:
  5V: 부품1.5V, hc-sr1.VCC
  GND: 부품1.GND, hc-sr1.GND
  N1: 부품1.D50, hc-sr1.Echo
  N2: 부품1.D51, hc-sr1.Trig
